// Logisim project Common bus system.circ as structural Verilog: 1 circuit, main circuit main
module main (
  input  [2:0] in_1,
  input  [3:0] INPUT,
  input  [2:0] SOURCE_SELECTION,
  output NO_REGISTER,
  output [3:0] out_5
);

  wire clock_1_out, decoder_1_out0, decoder_1_out1, decoder_1_out2, decoder_1_out3, decoder_1_out4,
       decoder_1_out5, decoder_1_out6;
  wire [3:0] multiplexer_1_out, multiplexer_2_out, multiplexer_4_out, multiplexer_6_out, multiplexer_7_out,
       multiplexer_9_out, multiplexer_11_out, register_1_q, register_2_q, register_3_q, register_4_q,
       register_5_q, register_6_q, register_7_q;

  Multiplexer #(.width(4)) multiplexer_1 (
    .in0(register_1_q), .in1(out_5), .out(multiplexer_1_out), .sel(decoder_1_out0));  // open: en
  Clock clock_1 (.out(clock_1_out));
  Register #(.width(4)) register_1 (.D(multiplexer_1_out), .Q(register_1_q), .clk(clock_1_out));  // open: en, clr
  Multiplexer #(.width(4)) multiplexer_2 (
    .in0(register_2_q), .in1(out_5), .out(multiplexer_2_out), .sel(decoder_1_out1));  // open: en
  Register #(.width(4)) register_2 (.D(multiplexer_2_out), .Q(register_2_q), .clk(clock_1_out));  // open: en, clr
  Multiplexer #(.select(3)) multiplexer_3 (
    .in0(register_1_q[0]), .in1(register_2_q[0]), .in2(register_3_q[0]), .in3(register_4_q[0]),
    .in4(register_5_q[0]), .in5(register_6_q[0]), .in6(register_7_q[0]), .in7(INPUT[0]), .out(out_5[0]),
    .sel(SOURCE_SELECTION));  // open: en
  Multiplexer #(.width(4)) multiplexer_4 (
    .in0(register_3_q), .in1(out_5), .out(multiplexer_4_out), .sel(decoder_1_out2));  // open: en
  Register #(.width(4)) register_3 (.D(multiplexer_4_out), .Q(register_3_q), .clk(clock_1_out));  // open: en, clr
  Multiplexer #(.select(3)) multiplexer_5 (
    .in0(register_1_q[1]), .in1(register_2_q[1]), .in2(register_3_q[1]), .in3(register_4_q[1]),
    .in4(register_5_q[1]), .in5(register_6_q[1]), .in6(register_7_q[1]), .in7(INPUT[1]), .out(out_5[1]),
    .sel(SOURCE_SELECTION));  // open: en
  Multiplexer #(.width(4)) multiplexer_6 (
    .in0(register_4_q), .in1(out_5), .out(multiplexer_6_out), .sel(decoder_1_out3));  // open: en
  Register #(.width(4)) register_4 (.D(multiplexer_6_out), .Q(register_4_q), .clk(clock_1_out));  // open: en, clr
  Multiplexer #(.width(4)) multiplexer_7 (
    .in0(register_5_q), .in1(out_5), .out(multiplexer_7_out), .sel(decoder_1_out4));  // open: en
  Register #(.width(4)) register_5 (.D(multiplexer_7_out), .Q(register_5_q), .clk(clock_1_out));  // open: en, clr
  Multiplexer #(.select(3)) multiplexer_8 (
    .in0(register_1_q[2]), .in1(register_2_q[2]), .in2(register_3_q[2]), .in3(register_4_q[2]),
    .in4(register_5_q[2]), .in5(register_6_q[2]), .in6(register_7_q[2]), .in7(INPUT[2]), .out(out_5[2]),
    .sel(SOURCE_SELECTION));  // open: en
  Multiplexer #(.width(4)) multiplexer_9 (
    .in0(register_6_q), .in1(out_5), .out(multiplexer_9_out), .sel(decoder_1_out5));  // open: en
  Multiplexer #(.select(3)) multiplexer_10 (
    .in0(register_1_q[3]), .in1(register_2_q[3]), .in2(register_3_q[3]), .in3(register_4_q[3]),
    .in4(register_5_q[3]), .in5(register_6_q[3]), .in6(register_7_q[3]), .in7(INPUT[3]), .out(out_5[3]),
    .sel(SOURCE_SELECTION));  // open: en
  Register #(.width(4)) register_6 (.D(multiplexer_9_out), .Q(register_6_q), .clk(clock_1_out));  // open: en, clr
  Multiplexer #(.width(4)) multiplexer_11 (
    .in0(register_7_q), .in1(out_5), .out(multiplexer_11_out), .sel(decoder_1_out6));  // open: en
  Register #(.width(4)) register_7 (.D(multiplexer_11_out), .Q(register_7_q), .clk(clock_1_out));  // open: en, clr
  Decoder #(.select(3)) decoder_1 (
    .out0(decoder_1_out0), .out1(decoder_1_out1), .out2(decoder_1_out2), .out3(decoder_1_out3),
    .out4(decoder_1_out4), .out5(decoder_1_out5), .out6(decoder_1_out6), .out7(NO_REGISTER), .sel(in_1));  // open: en

  // Notes on the sheet:
  //   COMMON 
  //   BUS
  //   INITIALLY TO LOAD INPUT INTO REGISTER
  //   SOURCE SELECTION MUST BE 111
  //   COMMON BUS SYSTEM
  //   DEBUG
  //   18BCE242 - Aditya Thakur
  //   18BCE248 - Utkarsh Pandya
  //   DESTINATION SELECTION
endmodule
