// Logisim project Serial Bus.circ as structural Verilog: 1 circuit, main circuit main
module main (
  input  [2:0] A_prime__B_prime__C_prime,
  input  [2:0] A__B__C,
  input  [3:0] INPUT_0,
  input  [3:0] INPUT_1,
  input  [3:0] INPUT_2,
  input  [3:0] INPUT_3,
  input  [3:0] INPUT_4,
  input  [3:0] INPUT_5,
  input  D,
  input  [2:0] A__B__C_2,
  output No_Register
);

  wire clock_1_out, decoder_1_out0, decoder_1_out1, decoder_1_out2, decoder_1_out3, decoder_1_out4,
       decoder_1_out5, decoder_1_out6, decoder_1_out7, decoder_2_out0, decoder_2_out1, decoder_2_out2,
       decoder_2_out3, decoder_2_out4, decoder_2_out5, decoder_2_out6, decoder_2_out7, multiplexer_1_out,
       or_1_out, or_3_out, or_4_out, or_5_out, or_6_out, or_7_out;
  wire [0:0] register_1_q, register_2_q, register_3_q, register_4_q, register_5_q, register_6_q;
  wire [2:0] register_1_q_2, register_2_q_2, register_3_q_2, register_4_q_2, register_6_q_2;
  wire [3:0] multiplexer_2_out, multiplexer_3_out, multiplexer_5_out, multiplexer_6_out, multiplexer_7_out,
       multiplexer_8_out, register_5_q_2;

  Decoder #(.select(3)) decoder_1 (
    .out0(decoder_1_out0), .out1(decoder_1_out1), .out2(decoder_1_out2), .out3(decoder_1_out3),
    .out4(decoder_1_out4), .out5(decoder_1_out5), .out6(decoder_1_out6), .out7(decoder_1_out7),
    .sel(A_prime__B_prime__C_prime));  // open: en
  Decoder #(.select(3)) decoder_2 (
    .out0(decoder_2_out0), .out1(decoder_2_out1), .out2(decoder_2_out2), .out3(decoder_2_out3),
    .out4(decoder_2_out4), .out5(decoder_2_out5), .out6(decoder_2_out6), .out7(decoder_2_out7), .sel(A__B__C));  // open: en
  or or_1 (or_1_out, decoder_1_out0, decoder_2_out0);
  Multiplexer multiplexer_1 (.in0(1'b0), .in1(or_1_out), .out(multiplexer_1_out), .sel(D));  // open: en
  Clock clock_1 (.out(clock_1_out));
  or or_2 (No_Register, decoder_1_out6, decoder_1_out7, decoder_2_out6, decoder_2_out7);
  Multiplexer #(.width(4)) multiplexer_2 (
    .in0(INPUT_0), .in1({register_5_q_2[3], register_1_q_2}), .out(multiplexer_2_out), .sel(multiplexer_1_out));  // open: en
  Register #(.width(4)) register_1 (
    .D(multiplexer_2_out), .Q({register_1_q_2, register_1_q[0]}), .clk(clock_1_out));  // open: en, clr
  or or_3 (or_3_out, decoder_2_out1, decoder_1_out1);
  Multiplexer #(.width(4)) multiplexer_3 (
    .in0(INPUT_1), .in1({register_5_q_2[3], register_2_q_2}), .out(multiplexer_3_out), .sel(or_3_out));  // open: en
  Register #(.width(4)) register_2 (
    .D(multiplexer_3_out), .Q({register_2_q_2, register_2_q[0]}), .clk(clock_1_out));  // open: en, clr
  or or_4 (or_4_out, decoder_1_out2, decoder_2_out2);
  Multiplexer #(.select(3)) multiplexer_4 (
    .in0(register_1_q[0]), .in1(register_2_q[0]), .in2(register_3_q[0]), .in3(register_4_q[0]),
    .in4(register_5_q[0]), .in5(register_6_q[0]), .out(register_5_q_2[3]), .sel(A__B__C_2));  // open: in6, in7, en
  Multiplexer #(.width(4)) multiplexer_5 (
    .in0(INPUT_2), .in1({register_5_q_2[3], register_3_q_2}), .out(multiplexer_5_out), .sel(or_4_out));  // open: en
  Register #(.width(4)) register_3 (
    .D(multiplexer_5_out), .Q({register_3_q_2, register_3_q[0]}), .clk(clock_1_out));  // open: en, clr
  or or_5 (or_5_out, decoder_1_out3, decoder_2_out3);
  Multiplexer #(.width(4)) multiplexer_6 (
    .in0(INPUT_3), .in1({register_5_q_2[3], register_4_q_2}), .out(multiplexer_6_out), .sel(or_5_out));  // open: en
  Register #(.width(4)) register_4 (
    .D(multiplexer_6_out), .Q({register_4_q_2, register_4_q[0]}), .clk(clock_1_out));  // open: en, clr
  or or_6 (or_6_out, decoder_1_out4, decoder_2_out4);
  Multiplexer #(.width(4)) multiplexer_7 (
    .in0(INPUT_4), .in1(register_5_q_2), .out(multiplexer_7_out), .sel(or_6_out));  // open: en
  Register #(.width(4)) register_5 (
    .D(multiplexer_7_out), .Q({register_5_q_2[2:0], register_5_q[0]}), .clk(clock_1_out));  // open: en, clr
  or or_7 (or_7_out, decoder_1_out5, decoder_2_out5);
  Multiplexer #(.width(4)) multiplexer_8 (
    .in0(INPUT_5), .in1({register_5_q_2[3], register_6_q_2}), .out(multiplexer_8_out), .sel(or_7_out));  // open: en
  Register #(.width(4)) register_6 (
    .D(multiplexer_8_out), .Q({register_6_q_2, register_6_q[0]}), .clk(clock_1_out));  // open: en, clr

  // Notes on the sheet:
  //   DESTINATION
  //   SELECTION
  //   SOURCE
  //   SELECTION
  //   COMMON BUS
  //   A  B  C - ARE USED TO SELECT SOURCE REGISTER
  //   A'  B'  C' - ARE USED TO SELECT DESTINATION  REGISTER
  //   INITIALLY FOR LOADING INPUT TO ANY REGISTER, 
  //   ALL THE VARIALBLES A, B, C, A', B', C', D MUST BE 0
  //   SERIAL BUS
  //   SOURCE  -  Circular Shift Operation
  //   DESTINATION - Shift Operation
  //   18BCE242 - ADITYA THAKUR
  //   18BCE248 - UTKARSH PANDYA
endmodule
